# Fritzing sketch air_quality_wiring_diagram (saved by Fritzing 0.9.3b)
breadboards: 1

parts:
  R1 = Resistor [tolerance=±5% resistance=4.7k package=THT]
  R2 = Resistor [tolerance=±5% resistance=4.7k package=THT]
  Part1 = Adafruit HUZZAH32 ESP32 Feather [part_number="Adafruit #3405"]  # not connected
  Part2 = Adafruit BME680
  Part3 = Adafruit CCS811

nets:
  N1: R1.Pin_0, Part2.SDI/SDA, Part3.SDA
  VIN: R1.Pin_1, R2.Pin_1, Part2.VIN, Part3.VIN
  N2: R2.Pin_0, Part2.SCK/SCL, Part3.SCL
  GND: Part2.GND, Part3.GND, Part3.!WAKE

notes:
  Pull-up Resistors, 4.7k
